# Fritzing sketch ModuleA (saved by Fritzing 0.9.3b)
stripboards: 35

parts:
  S1 = Round Pushbutton
  D1 = Rectifier Diode [part_number=1N4001 package="300 mil [THT]"]
  S2 = Round Pushbutton
  D2 = Rectifier Diode [part_number=1N4001 package="300 mil [THT]"]
  S3 = Round Pushbutton
  D3 = Rectifier Diode [part_number=1N4001 package="300 mil [THT]"]
  S5 = Round Pushbutton
  S4 = Round Pushbutton
  D4 = Rectifier Diode [part_number=1N4001 package="300 mil [THT]"]
  D5 = Rectifier Diode [part_number=1N4001 package="300 mil [THT]"]
  S8 = Round Pushbutton
  S6 = Round Pushbutton
  S9 = Round Pushbutton
  S10 = Round Pushbutton
  S7 = Round Pushbutton
  D7 = Rectifier Diode [part_number=1N4001 package="300 mil [THT]"]
  D9 = Rectifier Diode [part_number=1N4001 package="300 mil [THT]"]
  D8 = Rectifier Diode [part_number=1N4001 package="300 mil [THT]"]
  D10 = Rectifier Diode [part_number=1N4001 package="300 mil [THT]"]
  D6 = Rectifier Diode [part_number=1N4001 package="300 mil [THT]"]
  S13 = Round Pushbutton
  S11 = Round Pushbutton
  S14 = Round Pushbutton
  S15 = Round Pushbutton
  S12 = Round Pushbutton
  D12 = Rectifier Diode [part_number=1N4001 package="300 mil [THT]"]
  D14 = Rectifier Diode [part_number=1N4001 package="300 mil [THT]"]
  D13 = Rectifier Diode [part_number=1N4001 package="300 mil [THT]"]
  D15 = Rectifier Diode [part_number=1N4001 package="300 mil [THT]"]
  D11 = Rectifier Diode [part_number=1N4001 package="300 mil [THT]"]
  S16 = Round Pushbutton
  D16 = Rectifier Diode [part_number=1N4001 package="300 mil [THT]"]
  S20 = Round Pushbutton
  S21 = Round Pushbutton
  S17 = Round Pushbutton
  S19 = Round Pushbutton
  S18 = Round Pushbutton
  S22 = Round Pushbutton
  D17 = Rectifier Diode [part_number=1N4001 package="300 mil [THT]"]
  D18 = Rectifier Diode [part_number=1N4001 package="300 mil [THT]"]
  D22 = Rectifier Diode [part_number=1N4001 package="300 mil [THT]"]
  D20 = Rectifier Diode [part_number=1N4001 package="300 mil [THT]"]
  D19 = Rectifier Diode [part_number=1N4001 package="300 mil [THT]"]
  D21 = Rectifier Diode [part_number=1N4001 package="300 mil [THT]"]
  S23 = Round Pushbutton
  S25 = Round Pushbutton
  S27 = Round Pushbutton
  S28 = Round Pushbutton
  S26 = Round Pushbutton
  S24 = Round Pushbutton
  D26 = Rectifier Diode [part_number=1N4001 package="300 mil [THT]"]
  D27 = Rectifier Diode [part_number=1N4001 package="300 mil [THT]"]
  D23 = Rectifier Diode [part_number=1N4001 package="300 mil [THT]"]
  D25 = Rectifier Diode [part_number=1N4001 package="300 mil [THT]"]
  D28 = Rectifier Diode [part_number=1N4001 package="300 mil [THT]"]
  D24 = Rectifier Diode [part_number=1N4001 package="300 mil [THT]"]
  S29 = Round Pushbutton
  D29 = Rectifier Diode [part_number=1N4001 package="300 mil [THT]"]
  S32 = Round Pushbutton
  S31 = Round Pushbutton
  S30 = Round Pushbutton
  S34 = Round Pushbutton
  S33 = Round Pushbutton
  D30 = Rectifier Diode [part_number=1N4001 package="300 mil [THT]"]
  D33 = Rectifier Diode [part_number=1N4001 package="300 mil [THT]"]
  D32 = Rectifier Diode [part_number=1N4001 package="300 mil [THT]"]
  D34 = Rectifier Diode [part_number=1N4001 package="300 mil [THT]"]
  D31 = Rectifier Diode [part_number=1N4001 package="300 mil [THT]"]
  S35 = Round Pushbutton
  D35 = Rectifier Diode [part_number=1N4001 package="300 mil [THT]"]
  Part1 = Arduino Uno (Rev3)

nets:
  N1: S1.leg0, S2.leg0, S3.leg0, S5.leg0, S4.leg0, Part1.D5_PWM
  N2: S1.leg1, D1.anode
  N3: D1.cathode, D6.cathode, D12.cathode, D18.cathode, D25.cathode, D32.cathode, Part1.D8
  N4: S2.leg1, D2.anode
  N5: D2.cathode, D7.cathode, D13.cathode, D19.cathode, D26.cathode, D33.cathode, Part1.D9_PWM
  N6: S3.leg1, D3.anode
  N7: D3.cathode, D8.cathode, D14.cathode, D20.cathode, D27.cathode, D34.cathode, Part1.D10_PWM/SS
  N8: S5.leg1, D5.anode
  N9: S4.leg1, D4.anode
  N10: D4.cathode, D9.cathode, D15.cathode, D21.cathode, D28.cathode, Part1.D11_PWM/MOSI
  N11: D5.cathode, D10.cathode, D16.cathode, D22.cathode, D29.cathode, D35.cathode, Part1.D12/MISO
  N12: S8.leg0, S6.leg0, S9.leg0, S10.leg0, S7.leg0, Part1.D4
  N13: S8.leg1, D8.anode
  N14: S6.leg1, D6.anode
  N15: S9.leg1, D9.anode
  N16: S10.leg1, D10.anode
  N17: S7.leg1, D7.anode
  N18: S13.leg0, S11.leg0, S14.leg0, S15.leg0, S12.leg0, S16.leg0, Part1.D3_PWM
  N19: S13.leg1, D13.anode
  N20: S11.leg1, D11.anode
  N21: S14.leg1, D14.anode
  N22: S15.leg1, D15.anode
  N23: S12.leg1, D12.anode
  N24: D11.cathode, D17.cathode, D23.cathode, D30.cathode, Part1.D6_PWM
  N25: S16.leg1, D16.anode
  N26: S20.leg0, S21.leg0, S17.leg0, S19.leg0, S18.leg0, S22.leg0, Part1.D2
  N27: S20.leg1, D20.anode
  N28: S21.leg1, D21.anode
  N29: S17.leg1, D17.anode
  N30: S19.leg1, D19.anode
  N31: S18.leg1, D18.anode
  N32: S22.leg1, D22.anode
  N33: S23.leg0, S25.leg0, S27.leg0, S28.leg0, S26.leg0, S24.leg0, S29.leg0, Part1.D1/TX
  N34: S23.leg1, D23.anode
  N35: S25.leg1, D25.anode
  N36: S27.leg1, D27.anode
  N37: S28.leg1, D28.anode
  N38: S26.leg1, D26.anode
  N39: S24.leg1, D24.anode
  N40: D24.cathode, D31.cathode, Part1.D7
  N41: S29.leg1, D29.anode
  N42: S32.leg0, S31.leg0, S30.leg0, S34.leg0, S33.leg0, S35.leg0, Part1.D0/RX
  N43: S32.leg1, D32.anode
  N44: S31.leg1, D31.anode
  N45: S30.leg1, D30.anode
  N46: S34.leg1, D34.anode
  N47: S33.leg1, D33.anode
  N48: S35.leg1, D35.anode

notes:
  ModuleA - 35 keys
