# Fritzing sketch ModuleA_v2 (saved by Fritzing 0.9.3b)
stripboards: 2

parts:
  Part1 = Arduino Micro (Rev3)
  U1 = SWITCH-SPST-2 [package=switch-spst-vertical]
  S1 = Round Pushbutton
  S2 = Round Pushbutton
  S3 = Round Pushbutton
  S4 = Round Pushbutton
  S5 = Round Pushbutton
  S6 = Round Pushbutton
  S7 = Round Pushbutton
  S8 = Round Pushbutton
  S9 = Round Pushbutton
  S10 = Round Pushbutton
  S11 = Round Pushbutton
  S13 = Round Pushbutton
  S14 = Round Pushbutton
  S15 = Round Pushbutton
  S16 = Round Pushbutton
  S17 = Round Pushbutton
  S18 = Round Pushbutton
  S20 = Round Pushbutton
  S21 = Round Pushbutton
  S22 = Round Pushbutton
  S23 = Round Pushbutton
  S24 = Round Pushbutton
  S25 = Round Pushbutton
  S26 = Round Pushbutton
  S28 = Round Pushbutton
  S29 = Round Pushbutton
  S30 = Round Pushbutton
  S31 = Round Pushbutton
  S32 = Round Pushbutton
  S33 = Round Pushbutton
  D1 = Diode [package=diode-1n4148]
  D2 = Diode [package=diode-1n4148]
  D3 = Diode [package=diode-1n4148]
  D4 = Diode [package=diode-1n4148]
  D5 = Diode [package=diode-1n4148]
  D6 = Diode [package=diode-1n4148]
  D7 = Diode [package=diode-1n4148]
  D8 = Diode [package=diode-1n4148]
  D9 = Diode [package=diode-1n4148]
  D10 = Diode [package=diode-1n4148]
  D11 = Diode [package=diode-1n4148]
  D12 = Diode [package=diode-1n4148]
  D13 = Diode [package=diode-1n4148]
  D14 = Diode [package=diode-1n4148]
  D15 = Diode [package=diode-1n4148]
  D16 = Diode [package=diode-1n4148]
  D17 = Diode [package=diode-1n4148]
  D18 = Diode [package=diode-1n4148]
  D19 = Diode [package=diode-1n4148]
  D20 = Diode [package=diode-1n4148]
  D21 = Diode [package=diode-1n4148]
  D22 = Diode [package=diode-1n4148]
  D23 = Diode [package=diode-1n4148]
  D24 = Diode [package=diode-1n4148]
  D25 = Diode [package=diode-1n4148]
  D26 = Diode [package=diode-1n4148]
  D28 = Diode [package=diode-1n4148]
  D29 = Diode [package=diode-1n4148]
  D30 = Diode [package=diode-1n4148]
  D31 = Diode [package=diode-1n4148]

nets:
  N1: Part1.GND, U1.O
  N2: Part1.D2/SDA, S22.leg0, S23.leg0, S24.leg0, S25.leg0, S26.leg0
  N3: Part1.D3/SCL, S15.leg0, S16.leg0, S17.leg0, S18.leg0, S20.leg0, S21.leg0
  N4: Part1.D4_PWM/A6, S8.leg0, S9.leg0, S10.leg0, S11.leg0, S13.leg0, S14.leg0
  N5: Part1.D5_PWM, S1.leg0, S2.leg0, S3.leg0, S4.leg0, S5.leg0, S6.leg0, S7.leg0
  N6: Part1.D6_PWM/A7, S28.leg0, S29.leg0, S30.leg0, S31.leg0, S32.leg0, S33.leg0
  N7: Part1.D7, D1.A, D2.A, D3.A, D4.A
  N8: Part1.D8_PWM/A8, D5.A, D6.A
  N9: Part1.D9_PWM/A9, D7.A, D8.A, D9.A, D10.A, D11.A
  N10: Part1.D10_PWM/A10, D12.A, D13.A, D14.A, D15.A, D16.A
  N11: Part1.D11_PWM, D17.A, D18.A, D19.A, D20.A, D21.A
  N12: Part1.D12_PWM/A11, D23.A, D24.A, D25.A, D26.A
  N13: Part1.A0, U1.P
  N14: Part1.D13_PWM, D22.A, D28.A, D29.A, D30.A, D31.A
  N15: S1.leg1, D30.C
  N16: S2.leg1, D25.C
  N17: S3.leg1, D20.C
  N18: S4.leg1, D15.C
  N19: S5.leg1, D8.C
  N20: S6.leg1, D5.C
  N21: S7.leg1, D2.C
  N22: S8.leg1, D28.C
  N23: S9.leg1, D18.C
  N24: S10.leg1, D13.C
  N25: S11.leg1, D3.C
  N26: S13.leg1, D23.C
  N27: S14.leg1, D9.C
  N28: S15.leg1, D29.C
  N29: S16.leg1, D19.C
  N30: S17.leg1, D14.C
  N31: S18.leg1, D4.C
  N32: S20.leg1, D24.C
  N33: S21.leg1, D10.C
  N34: S22.leg1, D11.C
  N35: S23.leg1, D31.C
  N36: S24.leg1, D21.C
  N37: S25.leg1, D26.C
  N38: S26.leg1, D16.C
  N39: S28.leg1, D17.C
  N40: S29.leg1, D12.C
  N41: S30.leg1, D6.C
  N42: S31.leg1, D1.C
  N43: S32.leg1, D22.C
  N44: S33.leg1, D7.C
