# Fritzing sketch ModuleB (saved by Fritzing 0.9.3b)
stripboards: 2

parts:
  Part1 = Arduino Micro (Rev3)
  U1 = SWITCH-SPST-2 [package=switch-spst-vertical]
  S32 = Round Pushbutton
  D2 = Diode [package=diode-1n4148]
  S33 = Round Pushbutton
  D3 = Diode [package=diode-1n4148]
  S34 = Round Pushbutton
  D4 = Diode [package=diode-1n4148]
  S35 = Round Pushbutton
  D5 = Diode [package=diode-1n4148]
  S36 = Round Pushbutton
  D6 = Diode [package=diode-1n4148]
  S37 = Round Pushbutton
  S38 = Round Pushbutton
  S39 = Round Pushbutton
  S40 = Round Pushbutton
  S41 = Round Pushbutton
  D7 = Diode [package=diode-1n4148]
  D8 = Diode [package=diode-1n4148]
  D9 = Diode [package=diode-1n4148]
  D10 = Diode [package=diode-1n4148]
  D11 = Diode [package=diode-1n4148]
  S42 = Round Pushbutton
  S43 = Round Pushbutton
  S44 = Round Pushbutton
  S45 = Round Pushbutton
  S46 = Round Pushbutton
  S47 = Round Pushbutton
  S48 = Round Pushbutton
  S49 = Round Pushbutton
  S50 = Round Pushbutton
  S51 = Round Pushbutton
  D12 = Diode [package=diode-1n4148]
  D13 = Diode [package=diode-1n4148]
  D14 = Diode [package=diode-1n4148]
  D15 = Diode [package=diode-1n4148]
  D16 = Diode [package=diode-1n4148]
  D17 = Diode [package=diode-1n4148]
  D18 = Diode [package=diode-1n4148]
  D19 = Diode [package=diode-1n4148]
  D20 = Diode [package=diode-1n4148]
  D21 = Diode [package=diode-1n4148]
  S52 = Round Pushbutton
  S53 = Round Pushbutton
  S54 = Round Pushbutton
  S55 = Round Pushbutton
  D22 = Diode [package=diode-1n4148]
  D23 = Diode [package=diode-1n4148]
  D24 = Diode [package=diode-1n4148]
  D25 = Diode [package=diode-1n4148]
  S56 = Round Pushbutton
  S57 = Round Pushbutton
  S58 = Round Pushbutton
  S60 = Round Pushbutton
  D26 = Diode [package=diode-1n4148]
  D28 = Diode [package=diode-1n4148]
  D29 = Diode [package=diode-1n4148]
  D30 = Diode [package=diode-1n4148]
  S61 = Round Pushbutton
  S62 = Round Pushbutton
  S63 = Round Pushbutton
  S64 = Round Pushbutton
  D31 = Diode [package=diode-1n4148]
  D32 = Diode [package=diode-1n4148]
  D33 = Diode [package=diode-1n4148]
  D34 = Diode [package=diode-1n4148]

nets:
  N1: Part1.GND, U1.O
  N2: Part1.D2/SDA, S36.leg0, S38.leg0, S48.leg0, S50.leg0, S53.leg0, S57.leg0, S63.leg0
  N3: Part1.D3/SCL, S35.leg0, S37.leg0, S42.leg0, S47.leg0, S52.leg0, S56.leg0, S62.leg0
  N4: Part1.D4_PWM/A6, S32.leg0, S39.leg0, S45.leg0, S49.leg0, S55.leg0, S58.leg0
  N5: Part1.D5_PWM, S33.leg0, S40.leg0, S44.leg0, S46.leg0, S54.leg0, S64.leg0
  N6: Part1.D6_PWM/A7, S34.leg0, S41.leg0, S43.leg0, S51.leg0, S60.leg0, S61.leg0
  N7: Part1.D7, D22.A, D23.A, D24.A, D25.A
  N8: Part1.D8_PWM/A8, D12.A, D16.A, D17.A, D18.A, D21.A
  N9: Part1.D9_PWM/A9, D13.A, D14.A, D15.A, D19.A, D20.A
  N10: Part1.D10_PWM/A10, D7.A, D8.A, D9.A, D10.A, D11.A
  N11: Part1.D11_PWM, D2.A, D3.A, D4.A, D5.A, D6.A
  N12: Part1.D12_PWM/A11, D26.A, D28.A, D29.A, D30.A
  N13: Part1.A0, U1.P
  N14: Part1.D13_PWM, D31.A, D32.A, D33.A, D34.A
  N15: S32.leg1, D2.C
  N16: S33.leg1, D3.C
  N17: S34.leg1, D4.C
  N18: S35.leg1, D5.C
  N19: S36.leg1, D6.C
  N20: S37.leg1, D9.C
  N21: S38.leg1, D10.C
  N22: S39.leg1, D7.C
  N23: S40.leg1, D8.C
  N24: S41.leg1, D11.C
  N25: S42.leg1, D21.C
  N26: S43.leg1, D14.C
  N27: S44.leg1, D16.C
  N28: S45.leg1, D13.C
  N29: S46.leg1, D20.C
  N30: S47.leg1, D19.C
  N31: S48.leg1, D17.C
  N32: S49.leg1, D18.C
  N33: S50.leg1, D15.C
  N34: S51.leg1, D12.C
  N35: S52.leg1, D24.C
  N36: S53.leg1, D23.C
  N37: S54.leg1, D25.C
  N38: S55.leg1, D22.C
  N39: S56.leg1, D28.C
  N40: S57.leg1, D29.C
  N41: S58.leg1, D26.C
  N42: S60.leg1, D30.C
  N43: S61.leg1, D34.C
  N44: S62.leg1, D33.C
  N45: S63.leg1, D31.C
  N46: S64.leg1, D32.C
