# Fritzing sketch matrix (saved by Fritzing 0.9.3b)
circuit board: 8.46667cm x 5.64444cm
perfboards: 1

parts:
  S11 = Round Pushbutton
  D5 = Rectifier Diode [part_number=1N4001 package="300 mil [THT]"]
  S12 = Round Pushbutton
  D6 = Rectifier Diode [part_number=1N4001 package="300 mil [THT]"]
  S13 = Round Pushbutton
  D7 = Rectifier Diode [part_number=1N4001 package="300 mil [THT]"]
  S14 = Round Pushbutton
  S15 = Round Pushbutton
  S16 = Round Pushbutton
  D8 = Rectifier Diode [part_number=1N4001 package="300 mil [THT]"]
  D9 = Rectifier Diode [part_number=1N4001 package="300 mil [THT]"]
  D10 = Rectifier Diode [part_number=1N4001 package="300 mil [THT]"]
  S17 = Round Pushbutton
  S18 = Round Pushbutton
  S19 = Round Pushbutton
  D11 = Rectifier Diode [part_number=1N4001 package="300 mil [THT]"]
  D12 = Rectifier Diode [part_number=1N4001 package="300 mil [THT]"]
  D13 = Rectifier Diode [part_number=1N4001 package="300 mil [THT]"]
  Part1 = Arduino Uno (Rev3)

nets:
  N1: S11.leg0, S12.leg0, S13.leg0, Part1.D10_PWM/SS
  N2: S11.leg1, D5.anode
  N3: D5.cathode, D8.cathode, D11.cathode, Part1.D6_PWM
  N4: S12.leg1, D6.anode
  N5: D6.cathode, D9.cathode, D12.cathode, Part1.D5_PWM
  N6: S13.leg1, D7.anode
  N7: D7.cathode, D10.cathode, D13.cathode, Part1.D4
  N8: S14.leg0, S15.leg0, S16.leg0, Part1.D11_PWM/MOSI
  N9: S14.leg1, D8.anode
  N10: S15.leg1, D9.anode
  N11: S16.leg1, D10.anode
  N12: S17.leg0, S18.leg0, S19.leg0, Part1.D12/MISO
  N13: S17.leg1, D11.anode
  N14: S18.leg1, D12.anode
  N15: S19.leg1, D13.anode
